// Logisim project redux-V.circ as structural Verilog: 6 circuits, main circuit ALU_8bits
module main (
  output [7:0] out_1,
  output [7:0] out_2
);

  wire ALUSrc, and_1_out, and_3_out, and_4_out, AutoEn, branch, button_1_out, Clk, desvio, jump, MemtoReg,
       not_1_out, RAM_W, RegW, \var , zero;
  wire [1:0] multiplexer_5_out;
  wire [3:0] func;
  wire [7:0] adder_1_out, adder_2_out, alu_8bits_1_s, and_2_out, banco_registradores_1_a,
       banco_registradores_1_b, imm, multiplexer_1_out, multiplexer_2_out, multiplexer_3_out,
       multiplexer_4_out, multiplexer_6_out, multiplexer_7_out, not_2_out, PC_q, sb, sj;

  Clock #(.highDuration(2), .lowDuration(2)) clock_1 (.out(Clk));
  Adder adder_1 (.a(PC_q), .b(multiplexer_3_out), .out(adder_1_out), .cin(1'b0));  // open: cout
  Multiplexer #(.width(8)) multiplexer_1 (
    .in0(adder_1_out), .in1(banco_registradores_1_b), .out(multiplexer_1_out), .sel(and_1_out));
  Adder adder_2 (.a(PC_q), .b(8'h1), .out(adder_2_out), .cin(1'b0));  // open: cout
  Multiplexer #(.width(8)) multiplexer_2 (
    .in0(adder_2_out), .in1(multiplexer_1_out), .out(multiplexer_2_out), .sel(desvio));
  Multiplexer #(.width(8)) multiplexer_3 (.in0(multiplexer_4_out), .in1(sb), .out(multiplexer_3_out), .sel(branch));
  not not_1 (not_1_out, \var );
  and and_1 (and_1_out, not_1_out, branch);
  Register PC (.D(multiplexer_2_out), .en(1'b1), .clk(Clk), .Q(PC_q), .clr(button_1_out));
  Button button_1 (.out(button_1_out));
  Multiplexer #(.width(8)) multiplexer_4 (.in0(imm), .in1(sj), .out(multiplexer_4_out), .sel(\var ));
  ROM #(.addrWidth(4), .dataWidth(12)) rom_1 (
    .addr(out_2[7:4]), .data({func, ALUSrc, RegW, AutoEn, MemtoReg, jump, RAM_W, branch, \var }));
  dual_port_ram dual_port_ram_1 (
    .addr(banco_registradores_1_b), .d(banco_registradores_1_a), .w(RAM_W), .Clk(Clk), .pc(PC_q),
    .data(out_1), .instr(out_2));
  Multiplexer #(.width(2)) multiplexer_5 (.in0(out_2[3:2]), .in1(2'b00), .out(multiplexer_5_out), .sel(AutoEn));
  Multiplexer #(.width(8)) multiplexer_6 (.in0(alu_8bits_1_s), .in1(out_1), .out(multiplexer_6_out), .sel(MemtoReg));
  banco_registradores banco_registradores_1 (
    .C(multiplexer_6_out), .Clk(Clk), .rra(multiplexer_5_out), .En(RegW), .wr(multiplexer_5_out),
    .rrb(out_2[1:0]), .A(banco_registradores_1_a), .B(banco_registradores_1_b));
  signext signext_1 (.A(out_2[3:0]), .S(imm));
  assign and_2_out = {8{1'b1}} & not_2_out;  // AND_Gate and_2, 8 bits wide
  assign not_2_out = ~banco_registradores_1_a;  // NOT_Gate not_2, 8 bits wide
  Multiplexer #(.width(8)) multiplexer_7 (
    .in0(banco_registradores_1_b), .in1(imm), .out(multiplexer_7_out), .sel(ALUSrc));
  and and_3 (and_3_out, and_2_out[0], and_2_out[1], and_2_out[2], and_2_out[3], and_2_out[4], and_2_out[5], and_2_out[6], and_2_out[7]);
  not not_3 (zero, and_3_out);
  and and_4 (and_4_out, branch, and_3_out);
  ALU_8bits alu_8bits_1 (
    .A(banco_registradores_1_a), .B(multiplexer_7_out), .func(func), .S(alu_8bits_1_s));  // open: Zero
  variation variation_1 (.jie(out_2[3:0]), .r0(zero), .brzruie(out_2[3:0]), .sj(sj), .sb(sb));
  or or_1 (desvio, jump, and_4_out);

  // Notes on the sheet:
  //   contents of rom_1 (hex, n*v repeats v):
  //   2 8 50 4 e0 9 2e0 23 840 340 440 540 40 140 640 740
endmodule

module ALU_8bits (
  input  [7:0] A,
  input  [7:0] B,
  input  [3:0] func,
  output Zero,
  output [7:0] S
);

  wire or_2_out;
  wire [7:0] adder_1_out, and_1_out, multiplier_1_out, not_1_out, or_1_out, shifter_1_out, shifter_2_out,
       subtractor_1_out, xor_1_out;

  Adder adder_1 (.a(A), .b(B), .out(adder_1_out));  // open: cin, cout
  Subtractor subtractor_1 (.a(A), .b(B), .out(subtractor_1_out));  // open: bin, bout
  Multiplier #(.mode("twosComplement")) multiplier_1 (.a(A), .b(B), .out(multiplier_1_out));  // open: cin, cout
  assign and_1_out = A & B;  // AND_Gate and_1, 8 bits wide
  assign or_1_out = A | B;  // OR_Gate or_1, 8 bits wide
  assign xor_1_out = A ^ B;  // XOR_Gate xor_1, 8 bits wide
  Shifter shifter_1 (.in(A), .\dist (B[2:0]), .out(shifter_1_out));
  Shifter #(.shift("lr")) shifter_2 (.in(A), .\dist (B[2:0]), .out(shifter_2_out));
  assign not_1_out = ~B;  // NOT_Gate not_1, 8 bits wide
  Multiplexer #(.select(4), .width(8)) multiplexer_1 (
    .in0(adder_1_out), .in1(subtractor_1_out), .in2(multiplier_1_out), .in3(and_1_out), .in4(or_1_out),
    .in5(xor_1_out), .in6(shifter_1_out), .in7(shifter_2_out), .in8(not_1_out), .out(S), .sel(func));  // open: in9, in10, in11, in12, in13, in14, in15
  or or_2 (or_2_out, S[0], S[1], S[2], S[3], S[4], S[5], S[6], S[7]);
  not not_2 (Zero, or_2_out);
endmodule

module banco_registradores (
  input  [7:0] C,
  input  Clk,
  input  [1:0] rra,
  input  En,
  input  [1:0] wr,
  input  [1:0] rrb,
  output [7:0] A,
  output [7:0] B
);

  wire demultiplexer_1_out0, demultiplexer_1_out1, demultiplexer_1_out2, demultiplexer_1_out3;
  wire [7:0] register_1_q, register_2_q, register_3_q, register_4_q;

  Demultiplexer #(.select(2)) demultiplexer_1 (
    .out0(demultiplexer_1_out0), .out1(demultiplexer_1_out1), .out2(demultiplexer_1_out2),
    .out3(demultiplexer_1_out3), .in(En), .sel(wr));
  Register #(.trigger("falling")) register_1 (
    .D(C), .en(demultiplexer_1_out0), .clk(Clk), .Q(register_1_q));  // open: clr
  Register #(.trigger("falling")) register_2 (
    .D(C), .en(demultiplexer_1_out1), .clk(Clk), .Q(register_2_q));  // open: clr
  Register #(.trigger("falling")) register_3 (
    .D(C), .en(demultiplexer_1_out2), .clk(Clk), .Q(register_3_q));  // open: clr
  Register #(.trigger("falling")) register_4 (
    .D(C), .en(demultiplexer_1_out3), .clk(Clk), .Q(register_4_q));  // open: clr
  Multiplexer #(.select(2), .width(8)) multiplexer_1 (
    .in0(register_1_q), .in1(register_2_q), .in2(register_3_q), .in3(register_4_q), .out(A), .sel(rra));
  Multiplexer #(.select(2), .width(8)) multiplexer_2 (
    .in0(register_1_q), .in1(register_2_q), .in2(register_3_q), .in3(register_4_q), .out(B), .sel(rrb));
endmodule

module dual_port_ram (
  input  [7:0] addr,
  input  [7:0] d,
  input  w,
  input  Clk,
  input  [7:0] pc,
  output [7:0] data,
  output [7:0] instr
);

  ROM trabalho2_end ();  // open: addr, data
  RAM #(.asyncread("true"), .trigger("falling")) ram_1 (
    .addr(addr), .we(w), .oe(1'b1), .clk(Clk), .din(d), .dout(data));
  ROM rom_1 (.addr(pc), .data(instr));
  ROM trabalho1 ();  // open: addr, data

  // Notes on the sheet:
  //   contents of trabalho2_end (hex, n*v repeats v):
  //   d0 d5 da df 47 43 d4 65 45 c0 cc da d0 c1 78 d0 47 43 c4 d0 cd 3b 41 c8 47 42 cc 3b dd dc 4f d4 d0
  //   41 c8 d0 c1 58 da df 47 43 d4 d0 c1 a0 79 d0 47 43 c4 d0 cd 2b 47 41 cc 23 c8 d0 47 43 cc 3b dc dc
  //   4f d4 d0 c1 58 a0 10
  //   contents of rom_1 (hex, n*v repeats v):
  //   d0 d5 da df 47 43 d4 67 42 cc da d0 c1 78 d0 47 43 c4 d0 cd 3b 41 c8 47 42 cc 3b dd dc 4f d4 d0 41
  //   c8 d0 c1 58 da 47 43 d4 d0 c1 a0 79 d0 47 43 c4 d0 cd 2b 47 43 cc 23 c8 d0 47 43 cc 3b dd dc dc 4f
  //   d4 d0 c1 58 a0 10
  //   contents of trabalho1 (hex, n*v repeats v):
  //   d0 d5 da df 41 dc 47 42 d4 c0 c0 45 45 c8 d1 33 cf ca d9 3b d0 da df 41 df dc 2f d0 7 47 43 c4 d0 42
  //   df dc 2f cd d0 3b 41 c8 47 42 cc 3b d0 47 42 d4 41 c0 43 df cc d0 41 c8 d0 3 da df 47 43 d4 d0 df 42
  //   dc 2f 42 dc d0 7 47 43 c4 d0 df 42 dc 2f cd 2b 47 41 cc 23 c8 d0 47 43 cc 3b d0 47 42 d4 47 c0 c0 42
  //   df cc d0 3 43 cc d0 10
endmodule

module signext (
  input  [3:0] A,
  output [7:0] S
);


  assign S = {{5{A[3]}}, A[2:0]};
endmodule

module variation (
  input  [3:0] jie,
  input  r0,
  input  [3:0] brzruie,
  output [7:0] sj,
  output [7:0] sb
);

  wire adder_2_cout;
  wire [4:0] adder_1_out, adder_2_out, not_1_out, shifter_1_out, shifter_2_out;
  wire [5:5] adder_1_cout, not_2_out;
  wire [6:0] adder_4_out;

  Shifter #(.width(5)) shifter_1 (.in({1'b0, jie}), .\dist (3'b001), .out(shifter_1_out));
  Shifter #(.width(5)) shifter_2 (.in({1'b0, brzruie}), .\dist (3'b001), .out(shifter_2_out));
  Adder #(.width(5)) adder_1 (.a(shifter_1_out), .b(5'b01000), .out(adder_1_out), .cout(adder_1_cout[5]));  // open: cin
  Adder #(.width(5)) adder_2 (.a(shifter_1_out), .b(5'b01001), .out(adder_2_out), .cout(adder_2_cout));  // open: cin
  Adder #(.width(5)) adder_3 (.a(shifter_2_out), .b(5'b01000), .out(sb[4:0]), .cin(1'b0), .cout(sb[5]));
  assign not_1_out = ~adder_2_out;  // NOT_Gate not_1, 5 bits wide
  not not_2 (not_2_out[5], adder_2_cout);
  Adder #(.width(7)) adder_4 (
    .a({1'b1, not_2_out[5], not_1_out}), .b(7'b0000001), .out(adder_4_out));  // open: cin, cout
  Multiplexer #(.width(7)) multiplexer_1 (
    .in0({1'b0, adder_1_cout[5], adder_1_out}), .in1(adder_4_out), .out({sj[7], sj[5:0]}), .sel(1'b1));

  assign sb[7:6] = 2'b00;
  assign sj[6] = sj[7];
endmodule
