// Logisim project ALU_8bits.circ as structural Verilog: 1 circuit, main circuit main
module main (
);

  wire [2:0] func_p1;
  wire [7:0] A_p1, adder_1_out, and_1_out, B_p1, multiplexer_1_out, multiplier_1_out, or_1_out,
       subtractor_1_out, xor_1_out;

  // PortIO #(.direction("onlyinput")) A: pin names not known; wires that end beside it: A_p1
  // PortIO #(.direction("onlyinput")) B: pin names not known; wires that end beside it: B_p1, A_p1
  Adder adder_1 (.a(A_p1), .b(B_p1), .out(adder_1_out));  // open: cin, cout
  Subtractor subtractor_1 (.a(A_p1), .b(B_p1), .out(subtractor_1_out));  // open: bin, bout
  Multiplier #(.mode("twosComplement")) multiplier_1 (.a(A_p1), .b(B_p1), .out(multiplier_1_out));  // open: cin, cout
  assign and_1_out = A_p1 & B_p1;  // AND_Gate and_1, 8 bits wide
  assign or_1_out = A_p1 | B_p1;  // OR_Gate or_1, 8 bits wide
  assign xor_1_out = A_p1 ^ B_p1;  // XOR_Gate xor_1, 8 bits wide
  Multiplexer #(.select(3), .width(8)) multiplexer_1 (
    .in0(adder_1_out), .in1(subtractor_1_out), .in2(multiplier_1_out), .in3(and_1_out), .in4(or_1_out),
    .in5(xor_1_out), .out(multiplexer_1_out), .sel(func_p1));  // open: in6, in7
  // PortIO #(.direction("onlyinput"), .number(3)) func: pin names not known; wires that end beside it: func_p1
  // PortIO #(.direction("onlyOutput")) S: pin names not known; wires that end beside it: multiplexer_1_out
endmodule
