// Logisim project Shifter_8bits.circ as structural Verilog: 1 circuit, main circuit main
module main (
);

  wire sel;
  wire [7:0] A_p1, multiplexer_8_out;

  // PortIO #(.direction("onlyinput"), .number(2)) sel: pin names not known
  // PortIO #(.direction("onlyinput")) A: pin names not known; wires that end beside it: {A_p1[7:3], A_p1[3], A_p1[1:0]}, A_p1[3]
  Multiplexer multiplexer_1 (.in0(A_p1[7]), .in1(A_p1[6]), .out(multiplexer_8_out[7]), .sel(sel));
  Multiplexer multiplexer_2 (.in0(A_p1[6]), .in1(A_p1[5]), .out(multiplexer_8_out[6]), .sel(sel));
  Multiplexer multiplexer_3 (.in0(A_p1[5]), .in1(A_p1[4]), .out(multiplexer_8_out[5]), .sel(sel));
  Multiplexer multiplexer_4 (.in0(A_p1[4]), .in1(A_p1[3]), .out(multiplexer_8_out[4]), .sel(sel));
  Multiplexer multiplexer_5 (.in0(A_p1[3]), .in1(A_p1[3]), .out(multiplexer_8_out[3]), .sel(sel));
  Multiplexer multiplexer_6 (.in0(A_p1[3]), .in1(A_p1[1]), .out(multiplexer_8_out[2]), .sel(sel));
  Multiplexer multiplexer_7 (.in0(A_p1[1]), .in1(A_p1[0]), .out(multiplexer_8_out[1]), .sel(sel));
  Multiplexer multiplexer_8 (.in0(A_p1[0]), .in1(1'b0), .out(multiplexer_8_out[0]), .sel(sel));
  // PortIO #(.direction("onlyOutput")) S: pin names not known; wires that end beside it: multiplexer_8_out
endmodule
